# Fritzing sketch B28_sema (saved by Fritzing 0.9.3b)
breadboards: 1

parts:
  Arduino = Arduino Uno (Rev3)
  Driver2 = 28BYJ-48 Driver Module [part_number=ULN2003 package=THT]
  R2 = Rotary Potentiometer (Small) [maximum_resistance=100kΩ package=THT]  # not connected
  S1 = Momentary Switch [package=ksa_sealed_tac_switch]
  SM1 = 28BYJ-48 Stepper Motor [part_number=28BYJ-48]  # not connected

nets:
  N1: Arduino.D8, Driver2.IN4
  N2: Arduino.D9_PWM, Driver2.IN3
  N3: Arduino.D10_PWM/SS, Driver2.IN2
  N4: Arduino.D11_PWM/MOSI, Driver2.IN1
  N5: S1.1, S1.2
  N6: S1.3, S1.4

custom parts:
  28BYJ-48 Driver Module: Generic male header
  28BYJ-48 Stepper Motor: Unipolar Stepper Motor 28BYJ-48 Top coil - pink & orange Bottom coil - blue & yellow Common rail - red Connector pins: blue - pink - yellow - orange - red
